// Logisim project pc.circ as structural Verilog
module Somador1bit (
  input  in_1,
  input  in_2,
  output out_3,
  output out_4
);

  xor xor_1 (out_3, in_1, in_2);
  and and_1 (out_4, in_1, in_2);
endmodule

module ULA (
  input  [15:0] A,
  input  [15:0] B,
  input  [3:0] F,
  output [15:0] R
);

  wire not_1_out, or_1_out, or_2_out, or_3_out, or_4_out, or_5_out, or_6_out;
  wire [15:0] and_1_out, and_2_out, resultado_soma, resultado_subtracao;
  wire [15:15] not_2_out, not_3_out;

  not not_1 (not_1_out, F[0]);
  or or_1 (or_1_out, F[0], F[1]);
  or or_2 (or_2_out, F[2], F[3]);
  or or_3 (or_3_out, not_1_out, F[1]);
  or or_4 (or_4_out, or_3_out, or_5_out);
  or or_5 (or_5_out, F[2], F[3]);
  or or_6 (or_6_out, or_1_out, or_2_out);
  not not_2 (not_2_out[15], or_6_out);
  not not_3 (not_3_out[15], or_4_out);
  Adder #(.width(16)) adder_1 (.a(A), .b(B), .out(resultado_soma));  // open: cin, cout
  Subtractor #(.width(16)) subtractor_1 (.a(A), .b(B), .out(resultado_subtracao));  // open: bin, bout
  assign and_1_out = {16{not_3_out[15]}} & resultado_subtracao;  // AND_Gate and_1, 16 bits wide
  assign and_2_out = {16{not_2_out[15]}} & resultado_soma;  // AND_Gate and_2, 16 bits wide
  assign R = and_2_out | and_1_out;  // OR_Gate or_7, 16 bits wide
  Shifter #(.width(16), .shift("lr")) shifter_1 ();  // open: in, dist, out
  Shifter #(.width(16)) shifter_2 ();  // open: in, dist, out
  Multiplier #(.width(16)) multiplier_1 ();  // open: a, b, out, cin, cout
  Divider #(.width(16)) divider_1 ();  // open: a, b, out, upper, rem
  Comparator #(.width(16), .mode("unsigned")) comparator_1 ();  // open: a, b, gt, eq, lt
  // AND_Gate and_3 is placed but not wired
  // OR_Gate or_8 is placed but not wired
  // NOT_Gate not_4 is placed but not wired

  // Other names for the same wires on the sheet: b0 = F[0]; b1 = F[1]; b2 = F[2]; b3 = F[3]
endmodule
